# Fritzing sketch esp32-plant (saved by Fritzing 1.0.2b)

parts:
  ESP32 = ESP32S-HiLetgo [part_number=ESP32S-HiLetgo]
  MQ-135 = Gas Sensor Breakout Board
  DHT22 = DHT22 module

nets:
  N1: ESP32.3.3, DHT22.+
  N2: ESP32.GPIO35, MQ-135.AOUT
  N3: ESP32.GPIO27, DHT22.Out
  GND: ESP32.GND, MQ-135.GND, DHT22.-
  VIN: ESP32.VIN, MQ-135.5V

custom parts:
  ESP32S-HiLetgo: HiLetgo ESP-WROOM-32 ESP32 ESP-32S Development Board 2.4GHz Dual-Mode WiFi + Bluetooth Dual Cores Microcontroller The ESP32 integrated with Antenna switches, RF Balun, power amplifiers, low-noise amplifiers, filters, and management modules, and the entire solution occupies the least area of PCB. 2.4 GHz Wi-Fi plus Bluetooth dual-mode chip, with TSMC Ultra-low power consumption 40nm technology,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
  Gas Sensor Breakout Board: Gas sensor breakout board. Input voltage is 5V. Sensor output is available in analog and digital.
  DHT22 module: DHT22 module. Pins VCC Data GND.
